# Fritzing sketch ex11 (saved by Fritzing 0.9.2b)
breadboards: 1

parts:
  U1 = 555 Timer [package="SO8 [SMD]"]
  R1 = Resistor [tolerance=±5% resistance=10k package=THT]
  R2 = Resistor [tolerance=±5% resistance=10k package=THT]
  C1 = Tantalum Capacitor [capacitance=100µF package="100 mil [THT, tantalum]"]
  VCC1 = Battery block 9V
  LED1 = LED - 5mm [color="Red (633nm)" package="5 mm [THT]"]
  R3 = Resistor [tolerance=±5% resistance=470 package=THT]
  LED2 = LED - 5mm [color="Red (633nm)" package="5 mm [THT]"]
  R4 = Resistor [tolerance=±5% resistance=470 package=THT]

nets:
  N1: U1.Pin_1, C1.-, VCC1.-, LED1.cathode
  N2: U1.Pin_2, U1.Pin_6, R2.Pin_1
  N3: U1.Pin_3, R3.Pin_0, LED2.cathode
  N4: U1.Pin_4, U1.Pin_8, VCC1.+, R4.Pin_0
  N5: U1.Pin_7, R1.Pin_1
  N6: LED1.anode, R3.Pin_1
  N7: LED2.anode, R4.Pin_1
