# Fritzing sketch ex3 (saved by Fritzing 0.9.2b)
breadboards: 1

parts:
  VCC1 = Battery block 9V
  POT = Trimmer Potentiometer [maximum_resistance=10kΩ package=THT]
  R2 = Resistor [tolerance=±5% resistance=470 package="0805 [SMD]"]
  LED1 = LED - 5mm [color="Red (633nm)" package="5 mm [THT]"]

nets:
  N1: VCC1.-, LED1.cathode
  N2: VCC1.+, POT.leg1
  N3: POT.leg2, R2.Pin_0
  N4: R2.Pin_1, LED1.anode
