# Fritzing sketch ex4 (saved by Fritzing 0.9.2b)
breadboards: 1

parts:
  R1 = Resistor [tolerance=±5% resistance=470 package=THT]
  C1 = Ceramic Capacitor [capacitance=100µF package="100 mil [THT, multilayer]"]
  LED1 = LED - 5mm [color="Red (633nm)" package="5 mm [THT]"]
  S1 = Pushbutton [package="[SMD]"]
  VCC1 = Battery block 9V

nets:
  N1: R1.Pin_0, C1.1, S1.Pin_1, S1.Pin_2
  N2: R1.Pin_1, LED1.anode
  N3: C1.0, LED1.cathode, VCC1.-
  N4: S1.Pin_3, S1.Pin_4, VCC1.+
