# Fritzing sketch ex5 (saved by Fritzing 0.9.2b)
breadboards: 1

parts:
  BAT1 = BC9VPC [package=bc9vpc]
  R1 = Resistor [tolerance=±5% resistance=220 package=THT]
  D2 = Rectifier Diode [part_number=1N4001 package="300 mil [THT]"]
  LED1 = LED - 5mm [color="Red (633nm)" package="5 mm [THT]"]

nets:
  N1: BAT1.V+, R1.Pin_0
  N2: BAT1.V-, LED1.cathode
  N3: R1.Pin_1, D2.anode
  N4: D2.cathode, LED1.anode
