# Fritzing sketch ex6 (saved by Fritzing 0.9.2b)
breadboards: 1

parts:
  R1 = Resistor [tolerance=±5% resistance=470 package=THT]
  BAT1_9V = BC9VPC [package=bc9vpc]
  LED1 = LED - 5mm [color="Red (633nm)" package="5 mm [THT]"]
  S1 = SWITCH-MOMENTARY-2 [package=tactile_switch_tall]
  Q1 = NPN-Transistor [package="TO92 [THT]"]
  R2 = Resistor [tolerance=±5% resistance=10k package=THT]  # not connected

nets:
  N1: R1.Pin_0, BAT1_9V.V+
  N2: R1.Pin_1, LED1.anode
  N3: BAT1_9V.V-, S1.1, Q1.E
  N4: LED1.cathode, Q1.C
