# Fritzing sketch ex7 (saved by Fritzing 0.9.2b)
breadboards: 1

parts:
  VCC1 = Battery block 9V
  R2 = Resistor [tolerance=±5% resistance=10 package=THT]
  R3 = Resistor [tolerance=±5% resistance=47 package=THT]
  LED1 = LED - 5mm [color="Red (633nm)" package="5 mm [THT]"]
  R1 = Photocell (LDR) [package=THT]

nets:
  N1: VCC1.-, R2.Pin_1, LED1.cathode
  N2: VCC1.+, R1.pin_0
  N3: R2.Pin_0, R3.Pin_0, R1.pin_1
