# Fritzing sketch ex8 (saved by Fritzing 0.9.2b)
breadboards: 1

parts:
  R1 = Resistor [tolerance=±5% resistance=470 package=THT]
  LED1 = LED - 5mm [color="Red (633nm)" package="5 mm [THT]"]
  BC547 = NPN-Transistor [package="TO92 [THT]"]
  R3_LDR = Photocell (LDR) [package=THT]
  R2 = TRIMPOT [package=trimpot-3mm-2]
  VCC1 = Battery block 9V

nets:
  N1: R1.Pin_0, R3_LDR.pin_0, VCC1.+
  N2: LED1.cathode, BC547.C
  N3: BC547.E, R2.WIPER, VCC1.-
  N4: BC547.B, R3_LDR.pin_1, R2.CCW
