# Fritzing sketch ex9 (saved by Fritzing 0.9.2b)
breadboards: 1

parts:
  R1 = Resistor [tolerance=±5% resistance=470 package=THT]
  R2 = Resistor [tolerance=±5% resistance=10k package=THT]
  R3 = Resistor [tolerance=±5% resistance=470 package=THT]
  R4 = Resistor [tolerance=±5% resistance=10k package=THT]
  LED1 = LED - 5mm [color="Red (633nm)" package="5 mm [THT]"]
  C1 = Tantalum Capacitor [capacitance=100µF package="100 mil [THT, tantalum]"]
  BC547 = NPN-Transistor [package="TO92 [THT]"]
  BC547_2 = NPN-Transistor [package="TO92 [THT]"]
  C2 = Tantalum Capacitor [capacitance=100µF package="100 mil [THT, tantalum]"]
  BAT1 = BC9VPC [package=bc9vpc]
  LED2 = LED - 5mm [color="Red (633nm)" package="5 mm [THT]"]

nets:
  N1: R1.Pin_0, R3.Pin_0, BAT1.V+
  N2: R2.Pin_1, BC547.B, C2.-
  N3: R3.Pin_1, LED2.anode
  N4: R4.Pin_1, C1.-, BC547_2.B
  N5: LED1.cathode, C1.+, BC547.C
  N6: BC547.E, BC547_2.E, BAT1.V-
  N7: BC547_2.C, C2.+, LED2.cathode
